# Fritzing sketch Remate (saved by Fritzing 0.9.4)
breadboards: 2

parts:
  Part1 = Arduino Nano (Rev3.0)
  Q1 = TRANSISTOR_NPN [package=to-92]
  D1 = Rectifier Diode [part_number=1N4001 package="300 mil [THT]"]
  M1 = DC Motor
  M2 = DC Motor
  VCC1 = Battery block 9V
  M3 = DC Motor
  Q2 = TRANSISTOR_NPN [package=to-92]
  Q3 = TRANSISTOR_NPN [package=to-92]
  Q4 = TRANSISTOR_PNP [package=to-92]
  Q5 = TRANSISTOR_PNP [package=to-92]
  Q6 = TRANSISTOR_NPN [package=to-92]
  Q7 = TRANSISTOR_NPN [package=to-92]
  Q8 = TRANSISTOR_PNP [package=to-92]
  Q9 = TRANSISTOR_PNP [package=to-92]
  R8 = Resistor [tolerance=±5% resistance=220 package=THT]
  R1 = Resistor [tolerance=±5% resistance=220 package=THT]
  R9 = Resistor [tolerance=±5% resistance=220 package=THT]
  R7 = Resistor [tolerance=±5% resistance=220 package=THT]
  R6 = Resistor [tolerance=±5% resistance=220 package=THT]
  R5 = Resistor [tolerance=±5% resistance=220 package=THT]
  R4 = Resistor [tolerance=±5% resistance=220 package=THT]
  R3 = Resistor [tolerance=±5% resistance=220 package=THT]
  R2 = Resistor [tolerance=±5% resistance=220 package=THT]
  R10 = Resistor [tolerance=±5% resistance=10k package=THT]
  R11 = Resistor [tolerance=±5% resistance=10k package=THT]
  R12 = Resistor [tolerance=±5% resistance=10k package=THT]
  R13 = Resistor [tolerance=±5% resistance=10k package=THT]
  D6 = Rectifier Diode [part_number=1N4001 package="300 mil [THT]"]
  D7 = Rectifier Diode [part_number=1N4001 package="300 mil [THT]"]
  D8 = Rectifier Diode [part_number=1N4001 package="300 mil [THT]"]
  D9 = Rectifier Diode [part_number=1N4001 package="300 mil [THT]"]
  D10 = Rectifier Diode [part_number=1N4001 package="300 mil [THT]"]
  D11 = Rectifier Diode [part_number=1N4001 package="300 mil [THT]"]
  D12 = Rectifier Diode [part_number=1N4001 package="300 mil [THT]"]
  D13 = Rectifier Diode [part_number=1N4001 package="300 mil [THT]"]
  C1 = Ceramic Capacitor [capacitance=100nF package="200 mil [THT, multilayer]"]
  C2 = Capacitor Polarized [package=cpol-radial-10uf-25v]
  C4 = Ceramic Capacitor [capacitance=100nF package="200 mil [THT, multilayer]"]
  C6 = Capacitor Polarized [package=cpol-radial-10uf-25v]
  M4 = RioRand LM2596
  C9 = Ceramic Capacitor [capacitance=10nF package="200 mil [THT, multilayer]"]
  C10 = Ceramic Capacitor [capacitance=10nF package="200 mil [THT, multilayer]"]

nets:
  N1: Part1.GND, Q1.B, D1.anode, Q3.C, Q6.C, Q7.C, D9.anode, D12.anode, D13.anode, C1.0, C2.-, C4.0, C6.-, M4.Pin_4, C9.0, C10.0
  N2: Part1.D2, R2.Pin_1
  N3: Part1.D3, R3.Pin_1
  N4: Part1.D4, R4.Pin_1
  N5: Part1.D5, R5.Pin_1
  N6: Part1.D6, R6.Pin_1
  N7: Part1.D7, R7.Pin_1
  N8: Part1.D8, R9.Pin_1
  N9: Part1.D9, R8.Pin_1
  N10: Part1.D12/MISO, R1.Pin_0
  N11: Part1.5V, C1.1, C2.+, C4.1, C6.+
  N12: Part1.A1, C10.1
  N13: Part1.A0, C9.1
  N14: Q1.E, R1.Pin_1
  N15: Q1.C, M3.pin_1
  N16: D1.cathode, M3.pin_2, Q4.E, Q4.C, Q5.E, Q5.C, Q8.E, Q8.C, Q9.E, Q9.C, R7.Pin_0, R6.Pin_0, R3.Pin_0, R2.Pin_0, R10.Pin_0, R10.Pin_1, R11.Pin_0, R11.Pin_1, R12.Pin_0, R12.Pin_1, R13.Pin_0, R13.Pin_1, D6.cathode, D7.cathode, D10.cathode, D11.cathode, M4.Pin_3
  N17: M1.pin_1, Q3.B, Q5.B, D7.anode, D9.cathode
  N18: M1.pin_2, Q2.B, Q4.B, D6.anode, D8.cathode
  N19: M2.pin_1, Q6.B, Q9.B, D11.anode, D12.cathode
  N20: M2.pin_2, Q7.B, Q8.B, D10.anode, D13.cathode
  N21: VCC1.-, M4.Pin_2
  N22: VCC1.+, M4.Pin_1
  N23: Q2.E, R4.Pin_0
  N24: Q2.C, D8.anode
  N25: Q3.E, R5.Pin_0
  N26: Q6.E, R8.Pin_0
  N27: Q7.E, R9.Pin_0
