# Fritzing sketch Remate_v01 (saved by Fritzing 0.9.4)
breadboards: 1

parts:
  Part1 = Arduino Nano (Rev3.0)
  IC1 = L293D [package=THT]
  Q1 = TRANSISTOR_NPN [package=to-92]
  D1 = Rectifier Diode [part_number=1N4001 package="300 mil [THT]"]
  R1 = Resistor [tolerance=±5% resistance=220 package="0805 [SMD]"]
  M1 = DC Motor
  M2 = DC Motor
  VCC1 = Battery block 9V
  M3 = DC Motor

nets:
  N1: Part1.GND, IC1.0V, Q1.B, VCC1.-
  N2: Part1.D2, IC1.In_2
  N3: Part1.D4, IC1.In_1
  N4: Part1.D7, IC1.In_3
  N5: Part1.D8, IC1.In_4
  N6: Part1.D12/MISO, R1.Pin_0
  N7: Part1.5V, IC1.Enable_1, IC1.Enable_2, IC1.+V
  N8: IC1.Out_1_(_Controlled_by_Enable_1_), M1.pin_1
  N9: IC1.Out_2_(_Controlled_by_Enable_1_), M1.pin_2
  N10: IC1.+Vmotor, D1.cathode, VCC1.+, M3.pin_2
  N11: IC1.Out_3_(_Controlled_by_Enable_2_), M2.pin_2
  N12: IC1.Out_4_(_Controlled_by_Enable_2_), M2.pin_1
  N13: Q1.E, R1.Pin_1
  N14: Q1.C, M3.pin_1
